// Logisim project 7segments.circ as structural Verilog: 1 circuit, main circuit main
module main (
  input  w,
  input  x,
  input  y,
  input  z,
  output out_5,
  output out_6,
  output out_7,
  output out_8,
  output out_9,
  output out_10,
  output out_11
);

  wire and_1_out, and_2_out, and_3_out, and_4_out, and_5_out, and_6_out, and_7_out, and_8_out, and_9_out,
       and_10_out, and_11_out, and_12_out, and_13_out, and_14_out, and_15_out, and_16_out, and_17_out,
       and_18_out, and_19_out, and_20_out, and_21_out, and_22_out, and_23_out, and_24_out, and_25_out,
       and_26_out, and_27_out, and_28_out, and_29_out, and_30_out, and_31_out, and_32_out, and_33_out,
       and_34_out, and_35_out, and_36_out, and_37_out, and_38_out, and_39_out, not_1_out, not_2_out,
       not_3_out, not_4_out, not_5_out, not_6_out, not_7_out, not_8_out, not_9_out, not_10_out, not_11_out,
       not_12_out, not_13_out, not_14_out, not_15_out, not_16_out, not_17_out, not_18_out, not_19_out;

  _7_Segment_Display u_7_segment_display_1 (
    .g(out_11), .f(out_10), .a(out_5), .b(out_6), .e(out_9), .d(out_8), .c(out_7));  // open: dp
  not not_1 (not_1_out, w);
  not not_2 (not_2_out, x);
  not not_3 (not_3_out, y);
  not not_4 (not_4_out, z);
  not not_5 (not_5_out, w);
  not not_6 (not_6_out, x);
  not not_7 (not_7_out, y);
  not not_8 (not_8_out, z);
  not not_9 (not_9_out, w);
  not not_10 (not_10_out, x);
  not not_11 (not_11_out, y);
  not not_12 (not_12_out, z);
  not not_13 (not_13_out, w);
  not not_14 (not_14_out, x);
  not not_15 (not_15_out, y);
  not not_16 (not_16_out, z);
  not not_17 (not_17_out, y);
  not not_18 (not_18_out, x);
  not not_19 (not_19_out, z);
  and and_1 (and_1_out, w, not_14_out, not_15_out);
  and and_2 (and_2_out, w, not_16_out);
  and and_3 (and_3_out, x, y);
  and and_4 (and_4_out, not_14_out, not_16_out);
  and and_5 (and_5_out, not_13_out, y);
  and and_6 (and_6_out, not_13_out, x, z);
  and and_7 (and_7_out, not_13_out, not_14_out);
  and and_8 (and_8_out, not_14_out, not_15_out);
  and and_9 (and_9_out, not_13_out, not_15_out, not_16_out);
  and and_10 (and_10_out, w, not_15_out, z);
  and and_11 (and_11_out, not_13_out, y, z);
  and and_12 (and_12_out, w, not_14_out, not_16_out);
  and and_13 (and_13_out, not_13_out, x);
  and and_14 (and_14_out, w, not_14_out);
  and and_15 (and_15_out, not_13_out, not_15_out);
  and and_16 (and_16_out, not_13_out, z);
  and and_17 (and_17_out, not_15_out, z);
  and and_18 (and_18_out, w, not_3_out);
  and and_19 (and_19_out, not_1_out, not_2_out, not_4_out);
  and and_20 (and_20_out, x, not_3_out, z);
  and and_21 (and_21_out, not_2_out, y, z);
  and and_22 (and_22_out, x, y, not_4_out);
  and and_23 (and_23_out, x, y, not_4_out);
  and and_24 (and_24_out, w, x);
  and and_25 (and_25_out, w, y);
  and and_26 (and_26_out, y, not_19_out);
  and and_27 (and_27_out, w, y);
  and and_28 (and_28_out, not_18_out, not_17_out, not_19_out);
  and and_29 (and_29_out, not_6_out, w);
  and and_30 (and_30_out, not_7_out, not_8_out);
  and and_31 (and_31_out, w, y);
  and and_32 (and_32_out, not_5_out, not_7_out, x);
  and and_33 (and_33_out, not_5_out, not_8_out, x);
  and and_34 (and_34_out, y, not_12_out);
  and and_35 (and_35_out, w, not_10_out);
  and and_36 (and_36_out, w, z);
  and and_37 (and_37_out, w, y);
  and and_38 (and_38_out, not_10_out, y);
  and and_39 (and_39_out, not_9_out, x, not_11_out);
  or or_1 (out_7, and_13_out, and_14_out, and_15_out, and_16_out, and_17_out);
  or or_2 (out_5, and_1_out, and_2_out, and_3_out, and_4_out, and_5_out, and_6_out);
  or or_3 (out_6, and_7_out, and_8_out, and_9_out, and_10_out, and_11_out, and_12_out);
  or or_4 (out_8, and_18_out, and_19_out, and_20_out, and_21_out, and_22_out, and_23_out);
  or or_5 (out_9, and_24_out, and_25_out, and_26_out, and_27_out, and_28_out);
  or or_6 (out_10, and_30_out, and_29_out, and_31_out, and_32_out, and_33_out);
  or or_7 (out_11, and_34_out, and_35_out, and_36_out, and_37_out, and_38_out, and_39_out);
endmodule
