// Logisim project add complet.circ as structural Verilog: 1 circuit, main circuit main
module main (
  input  A,
  input  B,
  input  Rin,
  output Rout,
  output S
);

  wire and_1_out, and_2_out, and_3_out, and_4_out, and_5_out, and_6_out, and_7_out, not_1_out, not_2_out,
       not_3_out, not_4_out, not_5_out, not_6_out;

  not not_1 (not_1_out, Rin);
  and and_1 (and_1_out, A, B);
  and and_2 (and_2_out, B, Rin);
  not not_2 (not_2_out, B);
  not not_3 (not_3_out, Rin);
  not not_4 (not_4_out, A);
  not not_5 (not_5_out, B);
  not not_6 (not_6_out, A);
  and and_3 (and_3_out, A, Rin);
  and and_4 (and_4_out, A, not_2_out, not_3_out);
  and and_5 (and_5_out, not_4_out, not_5_out, Rin);
  and and_6 (and_6_out, A, B, Rin);
  and and_7 (and_7_out, not_6_out, B, not_1_out);
  or or_1 (Rout, and_1_out, and_3_out, and_2_out);
  or or_2 (S, and_4_out, and_5_out, and_6_out, and_7_out);
endmodule
